# Fritzing sketch polbreakout (saved by Fritzing 0.8.7b)
circuit board: 2.97718cm x 2.05106cm
breadboards: 1

parts:
  U2 = Voltage Regulator - 5V [package="TO220 [THT]"]
  R1 = Resistor [tolerance=±5% resistance=220 package=THT]
  R2 = Resistor [tolerance=±5% resistance=268 package=THT]
  J2 = Screw terminal - 2 pins [package=THT]
  J3 = Screw terminal - 2 pins [package=THT]
  U1 = YEV09T10 [package="5-SIP Module"]

nets:
  N1: U2.input_voltage, J2.pin2, U1.vin
  GND: U2.GND, R2.Pin_0, J2.pin1, J3.pin1, U1.gnd
  N2: U2.output_voltage, R1.Pin_0
  N3: R1.Pin_1, U1.on
  N4: R2.Pin_1, U1.trim
  N5: J3.pin2, U1.vout

custom parts:
  YEV09T10: 10A DC-DC POL Converter 4.5V to 13.8V Input 0.59V to 5.1V Output
